# Fritzing sketch Project 2 Fritzing (saved by Fritzing 0.9.3b)

parts:
  Raspberry_Pi_1 = Raspberry Pi 3 [part_number=RPI-3-V1.2]
  U1 = Graphical LCD 128x64 [package=lcd-g12864]
  J1 = Basic Servo
  Adafruit_HUZZAH_ESP8266_Breakout1 = Adafruit HUZZAH ESP8266 Breakout [part_number=2471]
  U2 = TCM8240MD [package=tcm8240md]  # not connected
  S1 = SPST Switch [package=switch-spdt-smd]
  R1 = Resistor [tolerance=±5% resistance=220 package=THT]

nets:
  N1: Raspberry_Pi_1.3v3, U1.K, S1.O
  N2: Raspberry_Pi_1.GIPO16, U1.VO, J1.pulse
  GND: Raspberry_Pi_1.GND, Raspberry_Pi_1.GIPO14, U1.DB0, U1.DB2, U1.E, J1.gnd, Adafruit_HUZZAH_ESP8266_Breakout1.GND, Adafruit_HUZZAH_ESP8266_Breakout1.TX
  N3: Raspberry_Pi_1.GIPO15, U1.D_I, Adafruit_HUZZAH_ESP8266_Breakout1.RX
  5V: Raspberry_Pi_1.5V, U1.A, J1.vcc, Adafruit_HUZZAH_ESP8266_Breakout1.V+
  N4: S1.P, R1.Pin_0

notes:
  Actual touch screen uses pins 1-26 (excluding pins 8 and 10)
  NFC
  Camera (uses a strip of wires)
  Micro Switch
